// Logisim project Muaz Kurt.circ as structural Verilog: 1 circuit, main circuit main
module main (
  input  in_1,
  input  [31:0] X,
  input  [31:0] Y,
  output [31:0] out_4
);

  wire and_1_out, and_2_out, and_3_out, and_4_out, and_5_out, and_6_out, clock_1_out, comparator_1_eq,
       comparator_1_gt, comparator_1_lt, decoder_1_out1, decoder_1_out3, decoder_1_out4, decoder_1_out5,
       not_1_out, not_2_out, not_3_out, not_4_out, or_1_out, or_2_out, or_3_out, or_4_out, or_5_out;
  wire [1:0] bit_extender_2_out;
  wire [2:0] bit_extender_1_out, register_1_q;
  wire [31:0] multiplexer_1_out, multiplexer_2_out, multiplexer_3_out, multiplexer_4_out, subtractor_1_out,
       X_q, Y_q;

  Clock clock_1 (.out(clock_1_out));
  Register #(.width(3)) register_1 (
    .D(bit_extender_1_out), .en(1'b1), .Q(register_1_q), .clk(clock_1_out));  // open: clr
  not not_1 (not_1_out, register_1_q[0]);
  not not_2 (not_2_out, register_1_q[2]);
  or or_1 (or_1_out, comparator_1_lt, comparator_1_eq);
  and and_1 (and_1_out, not_2_out, register_1_q[1], not_1_out, or_1_out);
  assign bit_extender_1_out = {{1{and_1_out}}, bit_extender_2_out};  // Bit_Extender bit_extender_1
  Multiplexer #(.width(32), .disabled(0), .enable("false")) multiplexer_1 (
    .in0(X), .in1(subtractor_1_out), .out(multiplexer_1_out), .sel(decoder_1_out3));
  and and_2 (and_2_out, not_1_out, comparator_1_gt, register_1_q[1]);
  Register #(.width(32)) u_X (.D(multiplexer_1_out), .en(or_4_out), .Q(X_q), .clk(clock_1_out));  // open: clr
  and and_3 (and_3_out, not_2_out, register_1_q[0]);
  and and_4 (and_4_out, register_1_q[2], not_1_out);
  or or_2 (or_2_out, and_2_out, and_4_out, and_3_out);
  assign bit_extender_2_out = {{1{or_2_out}}, or_3_out};  // Bit_Extender bit_extender_2
  Multiplexer #(.width(32), .disabled(0), .enable("false")) multiplexer_2 (
    .in0(Y), .in1(subtractor_1_out), .out(multiplexer_2_out), .sel(decoder_1_out4));
  Multiplexer #(.width(32), .disabled(0), .enable("false")) multiplexer_3 (
    .in0(X_q), .in1(Y_q), .out(multiplexer_3_out), .sel(comparator_1_lt));
  and and_5 (and_5_out, in_1, not_1_out, not_2_out, not_3_out);
  not not_3 (not_3_out, register_1_q[1]);
  and and_6 (and_6_out, not_1_out, not_4_out, register_1_q[1]);
  not not_4 (not_4_out, comparator_1_lt);
  Register #(.width(32)) u_Y (.D(multiplexer_2_out), .en(or_5_out), .Q(Y_q), .clk(clock_1_out));  // open: clr
  Multiplexer #(.width(32), .disabled(0), .enable("false")) multiplexer_4 (
    .in0(Y_q), .in1(X_q), .out(multiplexer_4_out), .sel(comparator_1_lt));
  Subtractor #(.width(32)) subtractor_1 (
    .a(multiplexer_3_out), .b(multiplexer_4_out), .out(subtractor_1_out));  // open: bin, bout
  or or_3 (or_3_out, and_6_out, and_5_out);
  Decoder #(.select(3), .enable("false")) decoder_1 (
    .out1(decoder_1_out1), .out3(decoder_1_out3), .out4(decoder_1_out4), .out5(decoder_1_out5),
    .sel(register_1_q));  // open: out0, out2, out6, out7
  Comparator #(.width(32), .mode("unsigned")) comparator_1 (
    .a(X_q), .b(Y_q), .gt(comparator_1_gt), .eq(comparator_1_eq), .lt(comparator_1_lt));
  Register #(.width(32)) register_2 (
    .D(multiplexer_3_out), .en(decoder_1_out5), .Q(out_4), .clk(clock_1_out));  // open: clr
  or or_4 (or_4_out, decoder_1_out1, decoder_1_out3);
  or or_5 (or_5_out, decoder_1_out1, decoder_1_out4);
endmodule
